# Fritzing sketch SaveTheDino (saved by Fritzing 0.8.7b)
circuit board: 8.46667cm x 5.64444cm
breadboards: 1

parts:
  Part1 = Arduino Uno (Rev3)
  R1 = PHOTOCELL [package=photocell]
  R2 = Resistor [tolerance=±5% resistance=10k package=THT]
  J1 = Basic Servo
  R3 = PHOTOCELL [package=photocell]
  R4 = Resistor [tolerance=±5% resistance=10k package=THT]

nets:
  N1: Part1.A0, R1.P$2, R2.Pin_0
  N2: Part1.A1, R3.P$2, R4.Pin_0
  N3: Part1.D9_PWM, J1.pulse
  GND: Part1.GND, R1.P$1, J1.gnd, R3.P$1
  5V: Part1.5V, R2.Pin_1, J1.vcc, R4.Pin_1
